// Logisim project Vrata_Version0.0.1.circ as structural Verilog: 6 circuits, main circuit main
module main (
);

  wire button_1_out, \functionality_1_otevírání , \functionality_1_otevřeno , \functionality_1_zavíraní ,
       \functionality_1_zavřeno ;

  Button button_1 (.out(button_1_out));
  LED led_1 (.in(\functionality_1_otevírání ));
  LED led_2 (.in(\functionality_1_otevřeno ));
  LED led_3 (.in(\functionality_1_zavřeno ));
  LED led_4 (.in(\functionality_1_zavíraní ));
  functionality functionality_1 (
    .Button(button_1_out), .\Otevírání (\functionality_1_otevírání ),
    .\Otevřeno (\functionality_1_otevřeno ), .\Zavíraní (\functionality_1_zavíraní ),
    .\Zavřeno (\functionality_1_zavřeno ));

  // Notes on the sheet:
  //   START/STOP
endmodule

module buttonswitch (
  input  Reset,
  input  Button,
  output \Output___Otevřeno_Zavřeno 
);

  wire d_ff_1_qn, d_ff_2_q, or_1_out;

  or or_1 (or_1_out, Button, Reset);
  D_Flip_Flop #(.trigger("high")) d_ff_1 (
    .clk(or_1_out), .D(d_ff_2_q), .Q(\Output___Otevřeno_Zavřeno ), .Qn(d_ff_1_qn));  // open: preset, en, reset
  D_Flip_Flop d_ff_2 (.clk(or_1_out), .D(d_ff_1_qn), .Q(d_ff_2_q));  // open: Qn, preset, en, reset
endmodule

module reset (
  input  Leva_Zavirani,
  input  Leva_Zavreno,
  input  Zavrit,
  input  CLOCK,
  output OUTPUT___RESET
);

  wire and_1_out;

  and and_1 (and_1_out, Leva_Zavirani, Leva_Zavreno, Zavrit);
  Counter #(.width(1), .max('h1), .trigger("falling")) counter_1 (
    .count(and_1_out), .carry(OUTPUT___RESET), .clk(CLOCK), .clr(OUTPUT___RESET));  // open: load, D, Q
endmodule

module functionality (
  input  Button,
  output \Otevírání ,
  output \Otevřeno ,
  output \Zavíraní ,
  output \Zavřeno 
);

  wire and_1_out, and_2_out, and_3_out, and_4_out, AR, AUTO_RESET, BR, clock_1_out, counter_3_carry, CR, LO,
       or_1_out, or_2_out, PO, VZ, ZT;
  wire [2:0] LH;

  Clock clock_1 (.out(clock_1_out));
  or or_1 (or_1_out, AUTO_RESET, BR);
  Button button_1 ();  // open: out
  buttonswitch buttonswitch_1 (.Reset(Button), .\Output___Otevřeno_Zavřeno (VZ), .Button(or_1_out));
  display display_1 (
    .\Pravá_Otevřeno (PO), .\Levá_otevřeno (LO), .\Zavřít (ZT), .Zapnuto_Vypnuto(VZ),
    .\Otevírání (\Otevírání ), .\Otevřeno (\Otevřeno ), .\Zavírání (\Zavíraní ), .\Zavřeno (\Zavřeno ));
  zavritdriv zavritdriv_1 (
    .Hodnota_otevreni_zleva(LH), .On_Off(VZ), .Zavrit_driv(AR), .Button_reset(BR), .Casovac_reset(CR),
    .Auto_Reset(AUTO_RESET));
  and and_1 (and_1_out, ZT, PO);
  and and_2 (and_2_out, VZ, clock_1_out);
  Counter #(.width(3), .max('h7), .ongoal("stay"), .trigger("falling")) counter_1 (
    .load(and_1_out), .Q(LH), .carry(LO), .clk(and_2_out));  // open: D, count, clr
  reset reset_1 (
    .Leva_Zavirani(LO), .Leva_Zavreno(and_1_out), .Zavrit(ZT), .OUTPUT___RESET(AUTO_RESET),
    .CLOCK(clock_1_out));
  and and_3 (and_3_out, LO, VZ, clock_1_out);
  Counter #(.width(3), .max('h7), .ongoal("stay"), .trigger("falling")) counter_2 (
    .load(ZT), .carry(PO), .clk(and_3_out));  // open: D, count, Q, clr
  and and_4 (and_4_out, PO, VZ, clock_1_out);
  Counter #(.width(3), .max('h7), .ongoal("stay")) counter_3 (
    .carry(counter_3_carry), .clk(and_4_out), .clr(or_2_out));  // open: load, D, count, Q
  or or_2 (or_2_out, CR, AUTO_RESET);
  or or_3 (ZT, counter_3_carry, AR);

  // Notes on the sheet:
  //   Hodnota otevření
endmodule

module display (
  input  \Pravá_Otevřeno ,
  input  \Levá_otevřeno ,
  input  \Zavřít ,
  input  Zapnuto_Vypnuto,
  output \Otevírání ,
  output \Otevřeno ,
  output \Zavírání ,
  output \Zavřeno 
);

  wire and_3_out, and_4_out, not_2_out, not_3_out, not_4_out, not_5_out, not_6_out;

  not not_1 (\Zavřeno , Zapnuto_Vypnuto);
  not not_2 (not_2_out, \Zavřít );
  not not_3 (not_3_out, \Pravá_Otevřeno );
  not not_4 (not_4_out, \Zavřít );
  not not_5 (not_5_out, \Pravá_Otevřeno );
  not not_6 (not_6_out, \Levá_otevřeno );
  and and_1 (\Otevírání , Zapnuto_Vypnuto, not_2_out, not_3_out);
  and and_2 (\Otevřeno , \Pravá_Otevřeno , not_4_out);
  and and_3 (and_3_out, not_5_out, \Zavřít );
  or or_1 (\Zavírání , and_3_out, and_4_out);
  and and_4 (and_4_out, not_6_out, \Zavřít );
endmodule

module zavritdriv (
  input  [2:0] Hodnota_otevreni_zleva,
  input  On_Off,
  input  Auto_Reset,
  output Zavrit_driv,
  output Button_reset,
  output Casovac_reset
);

  wire and_1_out, comparator_1_eq, comparator_1_gt, counter_1_carry, not_1_out, or_1_out;

  Counter #(.width(2), .max('h2), .ongoal("stay")) counter_1 (
    .carry(counter_1_carry), .clk(On_Off), .clr(or_1_out));  // open: load, D, count, Q
  or or_1 (or_1_out, Auto_Reset, and_1_out, Button_reset);
  and and_1 (and_1_out, not_1_out, counter_1_carry);
  not not_1 (not_1_out, On_Off);
  Comparator #(.width(3), .mode("unsigned")) comparator_1 (
    .a(Hodnota_otevreni_zleva), .b(3'b000), .gt(comparator_1_gt), .eq(comparator_1_eq));  // open: lt
  and and_2 (Zavrit_driv, comparator_1_gt, counter_1_carry);
  and and_3 (Button_reset, comparator_1_eq, counter_1_carry);
  or or_2 (Casovac_reset, Button_reset, and_1_out);
endmodule
