// Logisim project Vrata_Version0.2.0.circ as structural Verilog: 19 circuits, main circuit main
module main (
);

  wire _0_2_out, _0_out, _1, _1_2_out, _1_out, _2, _2_2_out, _2_out, _3, _3_2_out, _3_out, _4, _4_2_out,
       _4_out, _5, _5_2_out, _5_out, _6, _6_2_out, _6_out, _7, _7_2_out, _7_out, _8, _8_2_out, _8_out, _9,
       _9_2_out, _9_out, _10, _15, _16, _17, _18, _24, _26, C_out, cabelmanagment2_1_out_11,
       cabelmanagment2_1_out_12, locksystempassword_1_dioda, not_1_out, O_out, OK_2_out, OK_out;
  wire [2:0] locksystem_1__1__cifra, locksystem_1__1__cifra_2, locksystem_1__1__cifra_3,
       locksystem_1__2__cifra, locksystem_1__2__cifra_2, locksystem_1__2__cifra_3, locksystem_1__3__cifra,
       locksystem_1__3__cifra_2, locksystem_1__3__cifra_3, locksystem_1__4__cifra, locksystem_1__4__cifra_2,
       locksystem_1__4__cifra_3, locksystem_1_out_21, locksystem_1_out_22, locksystem_1_out_23,
       locksystem_1_out_24, locksystem_1_out_25, locksystem_1_out_26;
  wire [3:0] _1c, _2c, _3c, _4c, _11, _12, _13, _14, _25, cabelmanagment2_1_out_7, cabelmanagment2_1_out_8,
       cabelmanagment2_1_out_9, cabelmanagment2_1_out_10;
  wire [7:0] cardisplay_1_out_3, cardisplay_1_out_4, cardisplay_1_out_5, cardisplay_1_out_6,
       cardisplay_1_out_7, cardisplay_1_out_8, cardisplay_1_out_9, cardisplay_1_out_10, cardisplay_1_out_11,
       cardisplay_1_out_12, cardisplay_1_out_13, cardisplay_1_out_14, cardisplay_1_out_15,
       cardisplay_1_out_16, cardisplay_1_out_17, cardisplay_1_out_18, cardisplay_1_out_19,
       cardisplay_1_out_20, cardisplay_1_out_21, cardisplay_1_out_22, cardisplay_1_out_23,
       cardisplay_1_out_24, cardisplay_1_out_25, cardisplay_1_out_26, cardisplay_1_out_27,
       cardisplay_1_out_28, cardisplay_1_out_29, cardisplay_1_out_30;
  wire [15:0] _27, _28, _29, _30, _31, _32, _33, _34, _35, _36, _37, _38, _39, _40, _41, _42, _43, _44, _45,
       _46, _47, _48, _49, _50, _51, _52, _53, _54, _55, _56, _57, _58, cabelmanagment_1_out_17,
       cabelmanagment_1_out_18, cabelmanagment_1_out_19, cabelmanagment_1_out_20, cabelmanagment_1_out_21,
       cabelmanagment_1_out_22, cabelmanagment_1_out_23, cabelmanagment_1_out_24, cabelmanagment_1_out_25,
       cabelmanagment_1_out_26, cabelmanagment_1_out_27, cabelmanagment_1_out_28, cabelmanagment_1_out_29,
       cabelmanagment_1_out_30, cabelmanagment_1_out_31, cabelmanagment_1_out_32, cabelmanagment_2_out_17,
       cabelmanagment_2_out_18, cabelmanagment_2_out_19, cabelmanagment_2_out_20, cabelmanagment_2_out_21,
       cabelmanagment_2_out_22, cabelmanagment_2_out_23, cabelmanagment_2_out_24, cabelmanagment_2_out_25,
       cabelmanagment_2_out_26, cabelmanagment_2_out_27, cabelmanagment_2_out_28, cabelmanagment_2_out_29,
       cabelmanagment_2_out_30, cabelmanagment_2_out_31, cabelmanagment_2_out_32;
  wire [31:0] \statedisplay_1__1__řádek , \statedisplay_1__2__řádek , \statedisplay_1__3__řádek ,
       \statedisplay_1__4__řádek , \statedisplay_1__5__řádek ;

  Button S (.out(_15));
  Button button_1 (.out(_1));
  Button button_2 (.out(_2));
  DotMatrix #(.matrixcols(3), .matrixrows(3)) dotmatrix_1 (
    .col0(locksystem_1__2__cifra), .col1(locksystem_1__2__cifra_2), .col2(locksystem_1__2__cifra_3));
  DotMatrix #(.matrixcols(3), .matrixrows(3)) dotmatrix_2 (
    .col0(locksystem_1__1__cifra), .col1(locksystem_1__1__cifra_2), .col2(locksystem_1__1__cifra_3));
  DotMatrix #(.matrixcols(1), .matrixrows(3)) dotmatrix_3 (.col0(locksystem_1_out_26));
  Button C (.out(C_out));
  Button _0 (.out(_0_out));
  LockSystem locksystem_1 (
    ._7(_7_out), ._8(_8_out), ._9(_9_out), ._4(_4_out), ._5(_5_out), ._6(_6_out), ._1(_1_out), ._2(_2_out),
    ._3(_3_out), .C(C_out), ._0(_0_out), .OK(OK_out), .\Odemknuto_Zamčeno (_17), .Zavreno(_10),
    .out_21(locksystem_1_out_21), .out_22(locksystem_1_out_22), .out_23(locksystem_1_out_23),
    ._1__Cifra(locksystem_1__1__cifra), ._1__Cifra_2(locksystem_1__1__cifra_2),
    ._1__Cifra_3(locksystem_1__1__cifra_3), ._2__Cifra(locksystem_1__2__cifra),
    ._2__Cifra_2(locksystem_1__2__cifra_2), ._2__Cifra_3(locksystem_1__2__cifra_3),
    ._3__Cifra(locksystem_1__3__cifra), ._3__Cifra_2(locksystem_1__3__cifra_2),
    ._3__Cifra_3(locksystem_1__3__cifra_3), ._4__Cifra(locksystem_1__4__cifra),
    ._4__Cifra_2(locksystem_1__4__cifra_2), ._4__Cifra_3(locksystem_1__4__cifra_3), .out_19(_25),
    .Force_reset(_26), .out_26(locksystem_1_out_26), .out_25(locksystem_1_out_25),
    .out_24(locksystem_1_out_24), ._1C(_1c), ._2C(_2c), ._3C(_3c), ._4C(_4c));
  Button OK (.out(OK_out));
  Button P (.out(_16));
  Button button_3 (.out(_3));
  DotMatrix #(.matrixcols(3), .matrixrows(3)) dotmatrix_4 (
    .col0(locksystem_1__4__cifra), .col1(locksystem_1__4__cifra_2), .col2(locksystem_1__4__cifra_3));
  DotMatrix #(.matrixcols(1), .matrixrows(3)) dotmatrix_5 (.col0(locksystem_1_out_24));
  DotMatrix #(.matrixcols(3), .matrixrows(3)) dotmatrix_6 (
    .col0(locksystem_1__3__cifra), .col1(locksystem_1__3__cifra_2), .col2(locksystem_1__3__cifra_3));
  DotMatrix #(.matrixcols(1), .matrixrows(3)) dotmatrix_7 (.col0(locksystem_1_out_25));
  Button u__4 (.out(_4_out));
  Button u__2 (.out(_2_out));
  Button u__1 (.out(_1_out));
  Button u__3 (.out(_3_out));
  LED led_1 (.in(_4));
  LED led_2 (.in(_6));
  LED led_3 (.in(_5));
  DotMatrix #(.matrixcols(3), .matrixrows(3)) dotmatrix_8 (
    .col0(locksystem_1_out_21), .col1(locksystem_1_out_23), .col2(locksystem_1_out_22));
  Button u__5 (.out(_5_out));
  Button u__8 (.out(_8_out));
  Button u__6 (.out(_6_out));
  Button u__7 (.out(_7_out));
  DotMatrix #(.inputtype("row"), .matrixcols(32), .matrixrows(5)) dotmatrix_9 (
    .row0(\statedisplay_1__1__řádek ), .row1(\statedisplay_1__2__řádek ), .row2(\statedisplay_1__3__řádek ),
    .row3(\statedisplay_1__4__řádek ), .row4(\statedisplay_1__5__řádek ));
  DotMatrix #(.inputtype("row"), .matrixcols(16), .matrixrows(16)) dotmatrix_10 (
    .row0(cabelmanagment_1_out_17), .row1(cabelmanagment_1_out_18), .row2(cabelmanagment_1_out_19),
    .row3(cabelmanagment_1_out_20), .row4(cabelmanagment_1_out_21), .row5(cabelmanagment_1_out_22),
    .row6(cabelmanagment_1_out_23), .row7(cabelmanagment_1_out_24), .row8(cabelmanagment_1_out_25),
    .row9(cabelmanagment_1_out_26), .row10(cabelmanagment_1_out_27), .row11(cabelmanagment_1_out_28),
    .row12(cabelmanagment_1_out_29), .row13(cabelmanagment_1_out_30), .row14(cabelmanagment_1_out_31),
    .row15(cabelmanagment_1_out_32));
  Button u__9 (.out(_9_out));
  CabelManagment cabelmanagment_1 (
    .in_1(_27), .in_2(_28), .in_3(_29), .in_4(_30), .in_5(_31), .in_6(_32), .in_7(_33), .in_8(_34),
    .out_17(cabelmanagment_1_out_17), .out_18(cabelmanagment_1_out_18), .out_19(cabelmanagment_1_out_19),
    .out_20(cabelmanagment_1_out_20), .out_21(cabelmanagment_1_out_21), .out_22(cabelmanagment_1_out_22),
    .out_23(cabelmanagment_1_out_23), .out_24(cabelmanagment_1_out_24), .in_9(_35),
    .out_25(cabelmanagment_1_out_25), .in_10(_36), .out_26(cabelmanagment_1_out_26), .in_11(_37),
    .out_27(cabelmanagment_1_out_27), .in_12(_38), .out_28(cabelmanagment_1_out_28), .in_13(_39),
    .out_29(cabelmanagment_1_out_29), .in_14(_40), .out_30(cabelmanagment_1_out_30), .in_15(_41),
    .out_31(cabelmanagment_1_out_31), .in_16(_42), .out_32(cabelmanagment_1_out_32));
  Hex_Digit_Display hex_digit_display_1 (.value(cabelmanagment2_1_out_7));  // open: dp
  Hex_Digit_Display hex_digit_display_2 (.value(cabelmanagment2_1_out_8));  // open: dp
  StateDisplay statedisplay_1 (
    .\_1__Řádek (\statedisplay_1__1__řádek ), .\_2__Řádek (\statedisplay_1__2__řádek ),
    .\_3__Řádek (\statedisplay_1__3__řádek ), .\_4__Řádek (\statedisplay_1__4__řádek ),
    .\_5__Řádek (\statedisplay_1__5__řádek ), .\Otevřeno (_8), .\Zavřeno (_10), .\Otevírání (_7),
    .\Zavírání (_9));
  DotMatrix #(.inputtype("row"), .matrixcols(16), .matrixrows(16)) dotmatrix_11 (
    .row0(cabelmanagment_2_out_17), .row1(cabelmanagment_2_out_18), .row2(cabelmanagment_2_out_19),
    .row3(cabelmanagment_2_out_20), .row4(cabelmanagment_2_out_21), .row5(cabelmanagment_2_out_22),
    .row6(cabelmanagment_2_out_23), .row7(cabelmanagment_2_out_24), .row8(cabelmanagment_2_out_25),
    .row9(cabelmanagment_2_out_26), .row10(cabelmanagment_2_out_27), .row11(cabelmanagment_2_out_28),
    .row12(cabelmanagment_2_out_29), .row13(cabelmanagment_2_out_30), .row14(cabelmanagment_2_out_31),
    .row15(cabelmanagment_2_out_32));
  Hex_Digit_Display hex_digit_display_3 (.value(_25));  // open: dp
  CabelManagment cabelmanagment_2 (
    .in_1(_43), .in_2(_44), .in_3(_45), .in_4(_46), .in_5(_47), .in_6(_48), .in_7(_49), .in_8(_50),
    .out_17(cabelmanagment_2_out_17), .out_18(cabelmanagment_2_out_18), .out_19(cabelmanagment_2_out_19),
    .out_20(cabelmanagment_2_out_20), .out_21(cabelmanagment_2_out_21), .out_22(cabelmanagment_2_out_22),
    .out_23(cabelmanagment_2_out_23), .out_24(cabelmanagment_2_out_24), .in_9(_51),
    .out_25(cabelmanagment_2_out_25), .in_10(_52), .out_26(cabelmanagment_2_out_26), .in_11(_53),
    .out_27(cabelmanagment_2_out_27), .in_12(_54), .out_28(cabelmanagment_2_out_28), .in_13(_55),
    .out_29(cabelmanagment_2_out_29), .in_14(_56), .out_30(cabelmanagment_2_out_30), .in_15(_57),
    .out_31(cabelmanagment_2_out_31), .in_16(_58), .out_32(cabelmanagment_2_out_32));
  CabelManagment2 cabelmanagment2_1 (
    .in_1(_12), .in_2(_11), .in_3(_14), .in_4(_13), .in_5(_18), .in_6(_16), .out_7(cabelmanagment2_1_out_7),
    .out_8(cabelmanagment2_1_out_8), .out_9(cabelmanagment2_1_out_9), .out_10(cabelmanagment2_1_out_10),
    .out_11(cabelmanagment2_1_out_11), .out_12(cabelmanagment2_1_out_12));
  Hex_Digit_Display hex_digit_display_4 (.value(cabelmanagment2_1_out_9));  // open: dp
  Hex_Digit_Display hex_digit_display_5 (.value(cabelmanagment2_1_out_10));  // open: dp
  DotMatrix #(.matrixcols(13), .matrixrows(8)) dotmatrix_12 (
    .col0(cardisplay_1_out_3), .col1(cardisplay_1_out_6), .col2(cardisplay_1_out_9),
    .col3(cardisplay_1_out_11), .col4(cardisplay_1_out_13), .col5(cardisplay_1_out_15),
    .col6(cardisplay_1_out_17), .col7(cardisplay_1_out_19), .col8(cardisplay_1_out_21),
    .col9(cardisplay_1_out_23), .col10(cardisplay_1_out_25), .col11(cardisplay_1_out_27),
    .col12(cardisplay_1_out_29));
  CarDisplay cardisplay_1 (
    .out_3(cardisplay_1_out_3), .out_6(cardisplay_1_out_6), .out_9(cardisplay_1_out_9),
    .out_11(cardisplay_1_out_11), .out_13(cardisplay_1_out_13), .out_15(cardisplay_1_out_15),
    .out_17(cardisplay_1_out_17), .out_19(cardisplay_1_out_19), .out_21(cardisplay_1_out_21),
    .out_23(cardisplay_1_out_23), .out_25(cardisplay_1_out_25), .out_27(cardisplay_1_out_27),
    .out_29(cardisplay_1_out_29), .out_4(cardisplay_1_out_4), .out_7(cardisplay_1_out_7),
    .out_10(cardisplay_1_out_10), .out_12(cardisplay_1_out_12), .out_14(cardisplay_1_out_14),
    .out_16(cardisplay_1_out_16), .out_18(cardisplay_1_out_18), .out_20(cardisplay_1_out_20),
    .out_22(cardisplay_1_out_22), .out_24(cardisplay_1_out_24), .out_26(cardisplay_1_out_26),
    .out_28(cardisplay_1_out_28), .out_30(cardisplay_1_out_30), .in_1(cabelmanagment2_1_out_11),
    .in_2(cabelmanagment2_1_out_12), .out_5(cardisplay_1_out_5), .out_8(cardisplay_1_out_8));
  functionality functionality_1 (
    .Button(_15), .\Otevírání (_7), .\Otevřeno (_8), .\Zavíraní (_9), .\Zavřeno (_10), .Desitky(_12),
    .Jednotky(_11), .LED(_24), .LOW(_1), .MEDIUM(_2), .HIGH(_3), .HIGH_2(_6), .MEDIUM_2(_5), .LOW_2(_4),
    .Pustit_Auto(_16), .AUTO___Desitky(_14), .AUTO___Jednotky(_13), .Pustit_Auto_2(_18), .in_2(_17),
    .Row_1(_27), .out_15(_28), .out_17(_29), .out_19(_30), .out_20(_31), .out_21(_32), .out_23(_33),
    .out_24(_34), .out_25(_35), .out_27(_36), .out_28(_37), .out_29(_38), .out_30(_39), .out_31(_40),
    .out_32(_41), .Row_16(_42), .Row_1_2(_43), .out_36(_44), .out_37(_45), .out_39(_46), .out_40(_47),
    .out_42(_48), .out_43(_49), .out_44(_50), .out_45(_51), .out_46(_52), .out_47(_53), .out_48(_54),
    .out_49(_55), .out_50(_56), .out_51(_57), .Row_16_2(_58), .\Odemčeno (_17));
  DotMatrix #(.matrixcols(13), .matrixrows(8)) dotmatrix_13 (
    .col0(cardisplay_1_out_4), .col1(cardisplay_1_out_7), .col2(cardisplay_1_out_10),
    .col3(cardisplay_1_out_12), .col4(cardisplay_1_out_14), .col5(cardisplay_1_out_16),
    .col6(cardisplay_1_out_18), .col7(cardisplay_1_out_20), .col8(cardisplay_1_out_22),
    .col9(cardisplay_1_out_24), .col10(cardisplay_1_out_26), .col11(cardisplay_1_out_28),
    .col12(cardisplay_1_out_30));
  DotMatrix #(.matrixcols(2), .matrixrows(8)) dotmatrix_14 (.col0(cardisplay_1_out_5), .col1(cardisplay_1_out_8));
  not not_1 (not_1_out, _17);
  Button O (.out(O_out));
  Hex_Digit_Display hex_digit_display_6 (.value(_2c));  // open: dp
  Hex_Digit_Display hex_digit_display_7 (.value(_1c));  // open: dp
  Button OK_2 (.out(OK_2_out));
  Button _0_2 (.out(_0_2_out));
  Button _2_2 (.out(_2_2_out));
  Button _1_2 (.out(_1_2_out));
  Button button_4 (.out(_26));
  Hex_Digit_Display hex_digit_display_8 (.value(_4c));  // open: dp
  Hex_Digit_Display hex_digit_display_9 (.value(_3c));  // open: dp
  Button _4_2 (.out(_4_2_out));
  Button _3_2 (.out(_3_2_out));
  Button _5_2 (.out(_5_2_out));
  Button _6_2 (.out(_6_2_out));
  LED led_4 (.in(locksystempassword_1_dioda));
  Button _7_2 (.out(_7_2_out));
  Button _9_2 (.out(_9_2_out));
  LockSystemPassword locksystempassword_1 (
    .in_2(O_out), ._7(_7_2_out), ._8(_8_2_out), ._9(_9_2_out), ._4(_4_2_out), ._5(_5_2_out), ._6(_6_2_out),
    ._1(_1_2_out), ._2(_2_2_out), ._3(_3_2_out), ._0(_0_2_out), .OK(OK_2_out), ._1__Cifra(_1c),
    ._2__Cifra(_2c), ._3__Cifra(_3c), ._4__Cifra(_4c), .Dioda(locksystempassword_1_dioda),
    .\Zamčeno (not_1_out));
  Button _8_2 (.out(_8_2_out));

  // Notes on the sheet:
  //   VRÁTNICE
  //   START/STOP
  //   POMALU
  //   RYCHLEJI
  //   PUSTIT AUTO
  //   NEJRYCHLEJI
  //   HZ: 8
  //   RYCHLOSTI
  //   ČAS DO ZAVŘENÍ
  //   ZBÝVAJÍCÍ POKUSY
  //   POČET ČEKAJÍCÍCH AUT
  //   BOČNÍ KAMERA
  //   Odemčení
endmodule

module buttonswitch (
  input  Odemceno,
  input  Reset,
  input  Button,
  output \Output___Otevřeno_Zavřeno 
);

  wire and_1_out, d_ff_1_qn, d_ff_2_q, or_1_out;

  or or_1 (or_1_out, Button, Reset);
  and and_1 (and_1_out, or_1_out, Odemceno);
  D_Flip_Flop #(.trigger("high")) d_ff_1 (
    .clk(and_1_out), .D(d_ff_2_q), .Q(\Output___Otevřeno_Zavřeno ), .Qn(d_ff_1_qn));  // open: preset, en, reset
  D_Flip_Flop d_ff_2 (.clk(and_1_out), .D(d_ff_1_qn), .Q(d_ff_2_q));  // open: Qn, preset, en, reset
endmodule

module reset (
  input  Leva_Zavirani,
  input  Leva_Zavreno,
  input  Zavrit,
  input  CLOCK,
  output OUTPUT___RESET
);

  wire and_1_out;

  and and_1 (and_1_out, Leva_Zavirani, Leva_Zavreno, Zavrit);
  Counter #(.width(1), .max('h1), .trigger("falling")) counter_1 (
    .count(and_1_out), .carry(OUTPUT___RESET), .clk(CLOCK), .clr(OUTPUT___RESET));  // open: load, D, Q
endmodule

module functionality (
  input  Button,
  input  in_2,
  input  \Odemčeno ,
  input  LOW,
  input  MEDIUM,
  input  HIGH,
  input  Pustit_Auto,
  output [3:0] Desitky,
  output [3:0] Jednotky,
  output LED,
  output HIGH_2,
  output MEDIUM_2,
  output LOW_2,
  output \Otevírání ,
  output [15:0] out_15,
  output [15:0] Row_1,
  output [15:0] out_17,
  output \Otevřeno ,
  output [15:0] out_19,
  output [15:0] out_20,
  output [15:0] out_21,
  output \Zavíraní ,
  output [15:0] out_23,
  output [15:0] out_24,
  output [15:0] out_25,
  output \Zavřeno ,
  output [15:0] out_27,
  output [15:0] out_28,
  output [15:0] out_29,
  output [15:0] out_30,
  output [15:0] out_31,
  output [15:0] out_32,
  output [15:0] Row_16,
  output [15:0] Row_1_2,
  output [3:0] AUTO___Desitky,
  output [15:0] out_36,
  output [15:0] out_37,
  output Pustit_Auto_2,
  output [15:0] out_39,
  output [15:0] out_40,
  output [3:0] AUTO___Jednotky,
  output [15:0] out_42,
  output [15:0] out_43,
  output [15:0] out_44,
  output [15:0] out_45,
  output [15:0] out_46,
  output [15:0] out_47,
  output [15:0] out_48,
  output [15:0] out_49,
  output [15:0] out_50,
  output [15:0] out_51,
  output [15:0] Row_16_2
);

  wire and_1_out, and_2_out, and_3_out, and_4_out, and_5_out, and_6_out, AR, AUTO_RESET, BR, clock_1_out,
       clock_2_out, comparator_1_eq, comparator_2_gt, comparator_3_lt, counter_3_carry, CR, LO, not_1_out,
       or_1_out, or_2_out, PO, speedswitch_1_clock_output, VZ, ZP, ZT;
  wire [3:0] LH, PH;
  wire [4:0] counter_3_q;

  SpeedSwitch speedswitch_1 (
    .Clock_output(speedswitch_1_clock_output), .LOW(LOW), .MEDIUM(MEDIUM), .HIGH(HIGH), .HIGH_2(HIGH_2),
    .MEDIUM_2(MEDIUM_2), .LOW_2(LOW_2), .\Odemčeno (\Odemčeno ));
  Comparator #(.width(4), .mode("unsigned")) comparator_1 (.a(PH), .b(4'b1111), .eq(comparator_1_eq));  // open: gt, lt
  CarSystem carsystem_1 (
    .Button___Pustit(Pustit_Auto), .\Otevřeno (comparator_1_eq), .\Desítky (AUTO___Desitky),
    .Jednotky(AUTO___Jednotky), .Pusteni_povoleno(Pustit_Auto_2), .\Zavrení_povoleno (ZP),
    .\Zavřeno (\Zavřeno ));
  or or_1 (or_1_out, AUTO_RESET, BR);
  buttonswitch buttonswitch_1 (
    .Reset(Button), .\Output___Otevřeno_Zavřeno (VZ), .Button(or_1_out), .Odemceno(and_1_out));
  and and_1 (and_1_out, ZP, in_2);
  StateSystem statesystem_1 (
    .\Otevírání (\Otevírání ), .\Pravá_Otevřeno (PO), .\Otevřeno (\Otevřeno ), .\Levá_otevřeno (LO),
    .\Zavřít (ZT), .\Zavírání (\Zavíraní ), .Zapnuto_Vypnuto(VZ), .\Zavřeno (\Zavřeno ), .in_5(LH));
  and and_2 (and_2_out, and_5_out, comparator_3_lt);
  Counter #(.width(4), .max('hf), .ongoal("stay"), .trigger("falling")) counter_1 (
    .load(and_2_out), .Q(LH), .carry(LO), .clk(and_3_out));  // open: D, count, clr
  and and_3 (and_3_out, VZ, speedswitch_1_clock_output);
  reset reset_1 (
    .Leva_Zavirani(LO), .Leva_Zavreno(and_2_out), .Zavrit(and_5_out), .OUTPUT___RESET(AUTO_RESET),
    .CLOCK(speedswitch_1_clock_output));
  Comparator #(.width(4), .mode("unsigned")) comparator_2 (.a(LH), .b(4'b0101), .gt(comparator_2_gt));  // open: eq, lt
  GateDisplay gatedisplay_1 (
    .LEVA(LH), .out_5(out_15), .out_3(Row_1), .out_7(out_17), .out_9(out_19), .out_11(out_20),
    .out_13(out_21), .out_15(out_23), .out_17(out_24), .out_20(out_25), .out_22(out_27), .out_24(out_28),
    .out_26(out_29), .out_28(out_30), .out_30(out_31), .out_32(out_32), .out_34(Row_16), .out_4(Row_1_2),
    .out_6(out_36), .out_8(out_37), .out_10(out_39), .out_12(out_40), .out_14(out_42), .out_16(out_43),
    .out_18(out_44), .out_19(out_45), .out_21(out_46), .out_23(out_47), .out_25(out_48), .out_27(out_49),
    .out_29(out_50), .out_31(out_51), .out_33(Row_16_2), .PRAVA(PH));
  Counter #(.width(4), .max('hf), .ongoal("stay"), .trigger("falling")) counter_2 (
    .load(and_5_out), .Q(PH), .carry(PO), .clk(and_4_out));  // open: D, count, clr
  and and_4 (and_4_out, comparator_2_gt, VZ, speedswitch_1_clock_output);
  Comparator #(.width(4), .mode("unsigned")) comparator_3 (.a(PH), .b(4'b1000), .lt(comparator_3_lt));  // open: gt, eq
  and and_5 (and_5_out, ZT, ZP);
  Clock #(.highDuration(4), .lowDuration(4)) clock_1 (.out(clock_1_out));
  Counter #(.width(5), .max('h1e), .ongoal("stay")) counter_3 (
    .Q(counter_3_q), .carry(counter_3_carry), .clk(and_6_out), .clr(or_2_out));  // open: load, D, count
  or or_2 (or_2_out, CR, AUTO_RESET);
  and and_6 (and_6_out, PO, VZ, clock_1_out);
  or or_3 (ZT, counter_3_carry, AR);
  Clock #(.highDuration(3), .lowDuration(3)) clock_2 (.out(clock_2_out));
  and and_7 (LED, VZ, clock_2_out);
  CloseSystem closesystem_1 (
    .Hodnota_otevreni_zleva(LH), .On_Off(VZ), .Zavrit_driv(AR), .Button_reset(BR), .Casovac_reset(CR),
    .Auto_Reset(AUTO_RESET));
  not not_1 (not_1_out, AR);
  NumberDisplay numberdisplay_1 (
    .in_1(counter_3_q), .desitky(Desitky), .Jednotky(Jednotky), .in_2(not_1_out), .Zavreno_hlidani(\Zavíraní ));

  // Other names for the same wires on the sheet: Zavirani = \Zavíraní ; Zavreno = \Zavřeno 
endmodule

module StateSystem (
  input  \Pravá_Otevřeno ,
  input  \Levá_otevřeno ,
  input  \Zavřít ,
  input  Zapnuto_Vypnuto,
  input  [3:0] in_5,
  output \Otevírání ,
  output \Otevřeno ,
  output \Zavírání ,
  output \Zavřeno 
);

  wire and_2_out, and_3_out, and_4_out, and_6_out, comparator_1_eq, not_1_out, not_2_out, not_3_out,
       not_4_out, not_5_out;

  Comparator #(.width(4), .mode("unsigned")) comparator_1 (
    .a(in_5), .b(4'b0000), .eq(comparator_1_eq));  // open: gt, lt
  not not_1 (not_1_out, \Zavřít );
  not not_2 (not_2_out, \Pravá_Otevřeno );
  not not_3 (not_3_out, \Zavřít );
  not not_4 (not_4_out, \Pravá_Otevřeno );
  not not_5 (not_5_out, \Levá_otevřeno );
  and and_1 (\Otevírání , Zapnuto_Vypnuto, not_1_out, not_2_out);
  and and_2 (and_2_out, \Pravá_Otevřeno , not_3_out);
  and and_3 (and_3_out, not_4_out, \Zavřít );
  and and_4 (and_4_out, not_5_out, \Zavřít );
  and and_5 (\Zavřeno , ~Zapnuto_Vypnuto, comparator_1_eq);  // AND_Gate
  or or_1 (\Zavírání , and_3_out, and_4_out);
  or or_2 (\Otevřeno , and_2_out, and_6_out);
  and and_6 (and_6_out, ~\Otevírání , ~\Zavírání , ~\Zavřeno );  // AND_Gate
endmodule

module CloseSystem (
  input  [3:0] Hodnota_otevreni_zleva,
  input  On_Off,
  input  Auto_Reset,
  output Zavrit_driv,
  output Button_reset,
  output Casovac_reset
);

  wire and_1_out, comparator_1_eq, comparator_1_gt, counter_1_carry, or_1_out;

  and and_1 (and_1_out, ~On_Off, counter_1_carry);  // AND_Gate
  Comparator #(.width(4), .mode("unsigned")) comparator_1 (
    .a(Hodnota_otevreni_zleva), .b(4'b0000), .gt(comparator_1_gt), .eq(comparator_1_eq));  // open: lt
  Counter #(.width(2), .max('h2), .ongoal("stay")) counter_1 (
    .carry(counter_1_carry), .clk(On_Off), .clr(or_1_out));  // open: load, D, count, Q
  or or_1 (or_1_out, and_1_out, Button_reset, Auto_Reset);
  and and_2 (Zavrit_driv, comparator_1_gt, counter_1_carry);
  and and_3 (Button_reset, comparator_1_eq, counter_1_carry);
  or or_2 (Casovac_reset, Button_reset, and_1_out);
endmodule

module GateDisplay (
  input  [3:0] LEVA,
  input  [3:0] PRAVA,
  output [15:0] out_3,
  output [15:0] out_4,
  output [15:0] out_5,
  output [15:0] out_6,
  output [15:0] out_7,
  output [15:0] out_8,
  output [15:0] out_9,
  output [15:0] out_10,
  output [15:0] out_11,
  output [15:0] out_12,
  output [15:0] out_13,
  output [15:0] out_14,
  output [15:0] out_15,
  output [15:0] out_16,
  output [15:0] out_17,
  output [15:0] out_18,
  output [15:0] out_19,
  output [15:0] out_20,
  output [15:0] out_21,
  output [15:0] out_22,
  output [15:0] out_23,
  output [15:0] out_24,
  output [15:0] out_25,
  output [15:0] out_26,
  output [15:0] out_27,
  output [15:0] out_28,
  output [15:0] out_29,
  output [15:0] out_30,
  output [15:0] out_31,
  output [15:0] out_32,
  output [15:0] out_33,
  output [15:0] out_34
);

  DotMatrix #(.inputtype("row"), .matrixcols(16), .matrixrows(16)) dotmatrix_1 (
    .row0(16'h1f), .row1(16'h1f5), .row2(16'h755), .row3(16'h1d55), .row4(16'h1555), .row5(16'h7555),
    .row6(16'h5555), .row7(16'h5557), .row8(16'hd557), .row9(16'h9555), .row10(16'h9555), .row11(16'h9555),
    .row12(16'h9555), .row13(16'h9555), .row14(16'h9ddd), .row15(16'hf777));
  DotMatrix #(.inputtype("row"), .matrixcols(16), .matrixrows(16)) dotmatrix_2 (
    .row0(16'hf800), .row1(16'haf80), .row2(16'haae0), .row3(16'haab8), .row4(16'haaa8), .row5(16'haaae),
    .row6(16'haaaa), .row7(16'heaaa), .row8(16'heaab), .row9(16'haaa9), .row10(16'haaa9), .row11(16'haaa9),
    .row12(16'haaa9), .row13(16'haaa9), .row14(16'hbbb9), .row15(16'heeef));
  GateDisplaySystem gatedisplaysystem_1 (.in_1(16'h1f), .in_2(LEVA), .out_3(out_3));
  GateDisplaySystem gatedisplaysystem_2 (.in_1(16'h1f5), .in_2(LEVA), .out_3(out_5));
  GateDisplaySystem gatedisplaysystem_3 (.in_1(16'h755), .in_2(LEVA), .out_3(out_7));
  GateDisplaySystem gatedisplaysystem_4 (.in_1(16'h1d55), .in_2(LEVA), .out_3(out_9));
  GateDisplaySystem gatedisplaysystem_5 (.in_1(16'h1555), .in_2(LEVA), .out_3(out_11));
  GateDisplaySystem gatedisplaysystem_6 (.in_1(16'h7555), .in_2(LEVA), .out_3(out_13));
  GateDisplaySystem gatedisplaysystem_7 (.in_1(16'h5555), .in_2(LEVA), .out_3(out_15));
  GateDisplaySystem gatedisplaysystem_8 (.in_1(16'h5557), .in_2(LEVA), .out_3(out_17));
  GateDisplaySystem gatedisplaysystem_9 (.in_1(16'hd557), .in_2(LEVA), .out_3(out_20));
  GateDisplaySystem gatedisplaysystem_10 (.in_1(16'h9555), .in_2(LEVA), .out_3(out_22));
  GateDisplaySystem gatedisplaysystem_11 (.in_1(16'h9555), .in_2(LEVA), .out_3(out_24));
  GateDisplaySystem gatedisplaysystem_12 (.in_1(16'h9555), .in_2(LEVA), .out_3(out_26));
  GateDisplaySystem gatedisplaysystem_13 (.in_1(16'h9555), .in_2(LEVA), .out_3(out_28));
  GateDisplaySystem gatedisplaysystem_14 (.in_1(16'h9555), .in_2(LEVA), .out_3(out_30));
  GateDisplaySystem gatedisplaysystem_15 (.in_1(16'h9ddd), .in_2(LEVA), .out_3(out_32));
  GateDisplaySystem gatedisplaysystem_16 (.in_1(16'hf777), .in_2(LEVA), .out_3(out_34));
  GateDisplaySystem2 gatedisplaysystem2_1 (.in_1(16'hf800), .in_2(PRAVA), .out_3(out_4));
  GateDisplaySystem2 gatedisplaysystem2_2 (.in_1(16'haf80), .in_2(PRAVA), .out_3(out_6));
  GateDisplaySystem2 gatedisplaysystem2_3 (.in_1(16'haae0), .in_2(PRAVA), .out_3(out_8));
  GateDisplaySystem2 gatedisplaysystem2_4 (.in_1(16'haab8), .in_2(PRAVA), .out_3(out_10));
  GateDisplaySystem2 gatedisplaysystem2_5 (.in_1(16'haaa8), .in_2(PRAVA), .out_3(out_12));
  GateDisplaySystem2 gatedisplaysystem2_6 (.in_1(16'haaae), .in_2(PRAVA), .out_3(out_14));
  GateDisplaySystem2 gatedisplaysystem2_7 (.in_1(16'haaaa), .in_2(PRAVA), .out_3(out_16));
  GateDisplaySystem2 gatedisplaysystem2_8 (.in_1(16'heaaa), .in_2(PRAVA), .out_3(out_18));
  GateDisplaySystem2 gatedisplaysystem2_9 (.in_1(16'heaab), .in_2(PRAVA), .out_3(out_19));
  GateDisplaySystem2 gatedisplaysystem2_10 (.in_1(16'haaa9), .in_2(PRAVA), .out_3(out_21));
  GateDisplaySystem2 gatedisplaysystem2_11 (.in_1(16'haaa9), .in_2(PRAVA), .out_3(out_23));
  GateDisplaySystem2 gatedisplaysystem2_12 (.in_1(16'haaa9), .in_2(PRAVA), .out_3(out_25));
  GateDisplaySystem2 gatedisplaysystem2_13 (.in_1(16'haaa9), .in_2(PRAVA), .out_3(out_27));
  GateDisplaySystem2 gatedisplaysystem2_14 (.in_1(16'haaa9), .in_2(PRAVA), .out_3(out_29));
  GateDisplaySystem2 gatedisplaysystem2_15 (.in_1(16'hbbb9), .in_2(PRAVA), .out_3(out_31));
  GateDisplaySystem2 gatedisplaysystem2_16 (.in_1(16'heeef), .in_2(PRAVA), .out_3(out_33));
endmodule

module NumberDisplay (
  input  [4:0] in_1,
  input  in_2,
  input  Zavreno_hlidani,
  output [3:0] desitky,
  output [3:0] Jednotky
);

  wire [4:0] multiplexer_1_out, multiplexer_2_out, subtractor_1_out;
  wire [4:4] divider_1_out;

  Subtractor #(.width(5)) subtractor_1 (.a(5'b11110), .b(in_1), .out(subtractor_1_out));  // open: bin, bout
  Multiplexer #(.width(5), .enable("false")) multiplexer_1 (
    .in0(in_1), .in1({5{1'b0}}), .out(multiplexer_1_out), .sel(Zavreno_hlidani));
  Multiplexer #(.width(5), .enable("false")) multiplexer_2 (
    .in0(multiplexer_1_out), .in1(subtractor_1_out), .out(multiplexer_2_out), .sel(in_2));
  Divider #(.width(5)) divider_1 (
    .a(multiplexer_2_out), .b(5'b01010), .out({divider_1_out[4], desitky}), .rem({divider_1_out[4], Jednotky}));  // open: upper
  Hex_Digit_Display hex_digit_display_1 (.value(desitky));  // open: dp
  Hex_Digit_Display hex_digit_display_2 (.value(Jednotky));  // open: dp
  // also tied to GND on the sheet: divider_1_out[4]
endmodule

module StateDisplay (
  input  \Otevřeno ,
  input  \Zavřeno ,
  input  \Otevírání ,
  input  \Zavírání ,
  output [31:0] \_1__Řádek ,
  output [31:0] \_2__Řádek ,
  output [31:0] \_3__Řádek ,
  output [31:0] \_4__Řádek ,
  output [31:0] \_5__Řádek 
);

  assign \_1__Řádek  = \Zavírání  ? 32'hf32ae64a : 32'bz;  // Controlled_Buffer controlled_buffer_1
  assign \_1__Řádek  = \Otevírání  ? 32'heeeab925 : 32'bz;  // Controlled_Buffer controlled_buffer_2
  assign \_1__Řádek  = \Zavřeno  ? 32'hf32bba5e : 32'bz;  // Controlled_Buffer controlled_buffer_3
  assign \_1__Řádek  = \Otevřeno  ? 32'heeeaee97 : 32'bz;  // Controlled_Buffer controlled_buffer_4
  assign \_2__Řádek  = \Zavírání  ? 32'h24aaa96a : 32'bz;  // Controlled_Buffer controlled_buffer_5
  assign \_2__Řádek  = \Otevírání  ? 32'ha48aaab5 : 32'bz;  // Controlled_Buffer controlled_buffer_6
  assign \_2__Řádek  = \Zavřeno  ? 32'h24aaa352 : 32'bz;  // Controlled_Buffer controlled_buffer_7
  assign \_2__Řádek  = \Otevřeno  ? 32'ha48aa8d5 : 32'bz;  // Controlled_Buffer controlled_buffer_8
  assign \_3__Řádek  = \Zavírání  ? 32'h47aacf5a : 32'bz;  // Controlled_Buffer controlled_buffer_9
  assign \_3__Řádek  = \Otevírání  ? 32'ha4cab3ad : 32'bz;  // Controlled_Buffer controlled_buffer_10
  assign \_3__Řádek  = \Zavřeno  ? 32'h47ab32d2 : 32'bz;  // Controlled_Buffer controlled_buffer_11
  assign \_3__Řádek  = \Otevřeno  ? 32'ha4caccb5 : 32'bz;  // Controlled_Buffer controlled_buffer_12
  assign \_4__Řádek  = \Zavírání  ? 32'h84aaa95a : 32'bz;  // Controlled_Buffer controlled_buffer_13
  assign \_4__Řádek  = \Otevírání  ? 32'ha48aaaad : 32'bz;  // Controlled_Buffer controlled_buffer_14
  assign \_4__Řádek  = \Zavřeno  ? 32'h84aaa2d2 : 32'bz;  // Controlled_Buffer controlled_buffer_15
  assign \_4__Řádek  = \Otevřeno  ? 32'ha48aa8b5 : 32'bz;  // Controlled_Buffer controlled_buffer_16
  assign \_5__Řádek  = \Zavírání  ? 32'hf492a94a : 32'bz;  // Controlled_Buffer controlled_buffer_17
  assign \_5__Řádek  = \Otevírání  ? 32'he4e4aaa5 : 32'bz;  // Controlled_Buffer controlled_buffer_18
  assign \_5__Řádek  = \Zavřeno  ? 32'hf492ba5e : 32'bz;  // Controlled_Buffer controlled_buffer_19
  assign \_5__Řádek  = \Otevřeno  ? 32'he4e4ae97 : 32'bz;  // Controlled_Buffer controlled_buffer_20
  DotMatrix #(.inputtype("row"), .matrixcols(32), .matrixrows(5)) dotmatrix_1 (
    .row0(32'heeeaee97), .row1(32'ha48aa8d5), .row2(32'ha4caccb5), .row3(32'ha48aa8b5), .row4(32'he4e4ae97));
  DotMatrix #(.inputtype("row"), .matrixcols(32), .matrixrows(5)) dotmatrix_2 (
    .row0(32'hf32bba5e), .row1(32'h24aaa352), .row2(32'h47ab32d2), .row3(32'h84aaa2d2), .row4(32'hf492ba5e));
  DotMatrix #(.inputtype("row"), .matrixcols(32), .matrixrows(5)) dotmatrix_3 (
    .row0(32'heeeab925), .row1(32'ha48aaab5), .row2(32'ha4cab3ad), .row3(32'ha48aaaad), .row4(32'he4e4aaa5));
  DotMatrix #(.inputtype("row"), .matrixcols(32), .matrixrows(5)) dotmatrix_4 (
    .row0(32'hf32ae64a), .row1(32'h24aaa96a), .row2(32'h47aacf5a), .row3(32'h84aaa95a), .row4(32'hf492a94a));

  // Notes on the sheet:
  //   Otevřeno - Matrix text
  //   Zavřeno - Matrix Text
  //   Otevírání - Matrix Text
  //   Zavírání - Matrix Text
endmodule

module SpeedSwitch (
  input  HIGH,
  input  MEDIUM,
  input  LOW,
  input  \Odemčeno ,
  output Clock_output,
  output HIGH_2,
  output MEDIUM_2,
  output LOW_2
);

  wire and_1_out, and_2_out, and_3_out, and_4_out, clock_1_out, clock_2_out, clock_3_out, d_ff_1_qn,
       d_ff_2_q, d_ff_2_qn, d_ff_3_qn, or_1_out, or_2_out, or_3_out;
  wire [1:0] controlled_buffer_1_out;

  and and_1 (and_1_out, HIGH, \Odemčeno );
  and and_2 (and_2_out, MEDIUM, \Odemčeno );
  and and_3 (and_3_out, LOW, \Odemčeno );
  or or_1 (or_1_out, and_1_out, and_2_out, and_3_out);
  or or_2 (or_2_out, and_1_out, and_2_out, and_3_out);
  or or_3 (or_3_out, and_1_out, and_2_out, and_3_out);
  Clock clock_1 (.out(clock_1_out));
  Clock #(.highDuration(2), .lowDuration(2)) clock_2 (.out(clock_2_out));
  Clock #(.highDuration(4), .lowDuration(4)) clock_3 (.out(clock_3_out));
  D_Flip_Flop d_ff_1 (.clk(or_1_out), .D(and_1_out), .Q(HIGH_2), .Qn(d_ff_1_qn));  // open: preset, en, reset
  D_Flip_Flop d_ff_2 (.clk(or_2_out), .D(and_2_out), .Q(d_ff_2_q), .Qn(d_ff_2_qn));  // open: preset, en, reset
  D_Flip_Flop d_ff_3 (.clk(or_3_out), .D(and_3_out), .Q(LOW_2), .Qn(d_ff_3_qn));  // open: preset, en, reset
  and and_4 (and_4_out, d_ff_1_qn, d_ff_2_qn, d_ff_3_qn);
  Multiplexer #(.select(2), .enable("false")) multiplexer_1 (
    .in0(clock_1_out), .in1(clock_2_out), .in2(clock_3_out), .out(Clock_output), .sel(controlled_buffer_1_out));  // open: in3
  assign controlled_buffer_1_out = HIGH_2 ? 2'b00 : 2'bz;  // Controlled_Buffer controlled_buffer_1
  assign controlled_buffer_1_out = d_ff_2_q ? 2'b01 : 2'bz;  // Controlled_Buffer controlled_buffer_2
  assign controlled_buffer_1_out = LOW_2 ? 2'b10 : 2'bz;  // Controlled_Buffer controlled_buffer_3
  assign controlled_buffer_1_out = and_4_out ? 2'b01 : 2'bz;  // Controlled_Buffer controlled_buffer_4
  or or_4 (MEDIUM_2, d_ff_2_q, and_4_out);
endmodule

module CarSystem (
  input  Button___Pustit,
  input  \Otevřeno ,
  input  \Zavřeno ,
  output [3:0] \Desítky ,
  output [3:0] Jednotky,
  output Pusteni_povoleno,
  output \Zavrení_povoleno 
);

  wire and_1_out, CL, counter_1_carry, counter_3_carry, nor_1_out, or_1_out, or_3_out, xor_1_out, xor_2_out,
       xor_3_out, xor_4_out;
  wire [3:0] random_1_out;
  wire [4:0] counter_2_q;

  Clock #(.highDuration(3), .lowDuration(4)) clock_1 (.out(CL));
  Random #(.width(4)) random_1 (.clk(CL), .out(random_1_out));  // open: next, clr
  xor xor_1 (xor_1_out, random_1_out[0], 1'b1);
  xor xor_2 (xor_2_out, random_1_out[1], 1'b1);
  xor xor_3 (xor_3_out, random_1_out[2], 1'b1);
  xor xor_4 (xor_4_out, random_1_out[3], 1'b1);
  nor nor_1 (nor_1_out, xor_1_out, xor_2_out, xor_3_out, xor_4_out);
  and and_1 (and_1_out, or_3_out, Button___Pustit, \Otevřeno , counter_3_carry);
  or or_1 (or_1_out, nor_1_out, and_1_out);
  Counter #(.width(4), .max('h9), .ongoal("stay")) counter_1 (
    .carry(counter_1_carry), .clk(CL), .clr(and_1_out));  // open: load, D, count, Q
  Counter #(.width(5), .max('h1f), .ongoal("stay")) counter_2 (
    .load(and_1_out), .count(or_1_out), .Q(counter_2_q), .clk(or_1_out));  // open: D, carry, clr
  Counter #(.width(3), .max('h5), .ongoal("stay")) counter_3 (
    .carry(counter_3_carry), .clk(CL), .clr(and_1_out));  // open: load, D, count, Q
  NumberDisplay numberdisplay_1 (
    .in_1(counter_2_q), .desitky(\Desítky ), .Jednotky(Jednotky), .in_2(1'b0), .Zavreno_hlidani(1'b0));
  or or_2 (\Zavrení_povoleno , counter_1_carry, \Zavřeno );
  or or_3 (or_3_out, counter_2_q[0], counter_2_q[1], counter_2_q[2], counter_2_q[3], counter_2_q[4]);
  and and_2 (Pusteni_povoleno, counter_3_carry, or_3_out, \Otevřeno );
endmodule

module LockSystem (
  input  _7,
  input  _8,
  input  _9,
  input  _4,
  input  _5,
  input  _6,
  input  _1,
  input  _2,
  input  _3,
  input  C,
  input  _0,
  input  OK,
  input  [3:0] _1C,
  input  Force_reset,
  input  Zavreno,
  input  [3:0] _2C,
  input  [3:0] _3C,
  input  [3:0] _4C,
  output [3:0] out_19,
  output \Odemknuto_Zamčeno ,
  output [2:0] out_21,
  output [2:0] out_22,
  output [2:0] out_23,
  output [2:0] out_24,
  output [2:0] out_25,
  output [2:0] out_26,
  output [2:0] _1__Cifra,
  output [2:0] _1__Cifra_2,
  output [2:0] _1__Cifra_3,
  output [2:0] _2__Cifra,
  output [2:0] _2__Cifra_2,
  output [2:0] _2__Cifra_3,
  output [2:0] _3__Cifra,
  output [2:0] _3__Cifra_2,
  output [2:0] _3__Cifra_3,
  output [2:0] _4__Cifra,
  output [2:0] _4__Cifra_2,
  output [2:0] _4__Cifra_3
);

  wire and_1_out, and_2_out, comparator_1_eq, comparator_2_eq, comparator_3_eq, comparator_4_eq,
       counter_2_carry, demultiplexer_1_out0, demultiplexer_1_out1, demultiplexer_1_out2,
       demultiplexer_1_out3, Limit, or_1_out, or_2_out, or_3_out, or_4_out, or_5_out, or_6_out, or_7_out,
       s_r_ff_1_q, s_r_ff_2_q, s_r_ff_3_q, s_r_ff_4_q;
  wire [1:0] counter_1_q, counter_2_q;
  wire [3:0] controlled_buffer_1_out, n4bitmemory_1_out_5, n4bitmemory_2_out_5, n4bitmemory_3_out_5,
       n4bitmemory_4_out_5;

  or or_1 (or_1_out, C, OK);
  or or_2 (or_2_out, _2, _1, _4, _7, _0, _5, _8, _3, _6, _9);
  assign controlled_buffer_1_out = _9 ? 4'b1001 : 4'bz;  // Controlled_Buffer controlled_buffer_1
  assign controlled_buffer_1_out = _8 ? 4'b1000 : 4'bz;  // Controlled_Buffer controlled_buffer_2
  assign controlled_buffer_1_out = _7 ? 4'b0111 : 4'bz;  // Controlled_Buffer controlled_buffer_3
  assign controlled_buffer_1_out = _6 ? 4'b0110 : 4'bz;  // Controlled_Buffer controlled_buffer_4
  assign controlled_buffer_1_out = _5 ? 4'b0101 : 4'bz;  // Controlled_Buffer controlled_buffer_5
  assign controlled_buffer_1_out = _4 ? 4'b0100 : 4'bz;  // Controlled_Buffer controlled_buffer_6
  assign controlled_buffer_1_out = _3 ? 4'b0011 : 4'bz;  // Controlled_Buffer controlled_buffer_7
  assign controlled_buffer_1_out = _2 ? 4'b0010 : 4'bz;  // Controlled_Buffer controlled_buffer_8
  assign controlled_buffer_1_out = _1 ? 4'b0001 : 4'bz;  // Controlled_Buffer controlled_buffer_9
  assign controlled_buffer_1_out = _0 ? 4'b0000 : 4'bz;  // Controlled_Buffer controlled_buffer_10
  Demultiplexer #(.select(2), .enable("false")) demultiplexer_1 (
    .out0(demultiplexer_1_out0), .out1(demultiplexer_1_out1), .out2(demultiplexer_1_out2),
    .out3(demultiplexer_1_out3), .in(1'b1), .sel(counter_1_q));
  Counter #(.width(2), .max('h3), .ongoal("stay"), .trigger("falling")) counter_1 (
    .Q(counter_1_q), .clk(or_2_out), .clr(or_1_out));  // open: load, D, count, carry
  _4bitmemory u_4bitmemory_1 (
    .out_5(n4bitmemory_1_out_5), .Input(controlled_buffer_1_out), .Select(demultiplexer_1_out0),
    .Write(or_2_out), .RESET(or_1_out));
  _4bitmemory u_4bitmemory_2 (
    .out_5(n4bitmemory_2_out_5), .Input(controlled_buffer_1_out), .Select(demultiplexer_1_out1),
    .Write(or_2_out), .RESET(or_1_out));
  _4bitmemory u_4bitmemory_3 (
    .out_5(n4bitmemory_3_out_5), .Input(controlled_buffer_1_out), .Select(demultiplexer_1_out2),
    .Write(or_2_out), .RESET(or_1_out));
  _4bitmemory u_4bitmemory_4 (
    .out_5(n4bitmemory_4_out_5), .Input(controlled_buffer_1_out), .Select(demultiplexer_1_out3),
    .Write(or_2_out), .RESET(or_1_out));
  Comparator #(.width(4), .mode("unsigned")) comparator_1 (
    .a(_1C), .b(n4bitmemory_1_out_5), .eq(comparator_1_eq));  // open: gt, lt
  Comparator #(.width(4), .mode("unsigned")) comparator_2 (
    .a(_2C), .b(n4bitmemory_2_out_5), .eq(comparator_2_eq));  // open: gt, lt
  Comparator #(.width(4), .mode("unsigned")) comparator_3 (
    .a(_3C), .b(n4bitmemory_3_out_5), .eq(comparator_3_eq));  // open: gt, lt
  Comparator #(.width(4), .mode("unsigned")) comparator_4 (
    .a(_4C), .b(n4bitmemory_4_out_5), .eq(comparator_4_eq));  // open: gt, lt
  or or_3 (or_3_out, demultiplexer_1_out0, or_1_out);
  or or_4 (or_4_out, demultiplexer_1_out1, or_1_out);
  or or_5 (or_5_out, demultiplexer_1_out2, or_1_out);
  or or_6 (or_6_out, demultiplexer_1_out3, or_1_out);
  S_R_Flip_Flop #(.trigger("high")) s_r_ff_1 (
    .S(or_2_out), .clk(or_3_out), .R(or_1_out), .Q(s_r_ff_1_q));  // open: Qn, preset, reset, en
  S_R_Flip_Flop #(.trigger("high")) s_r_ff_2 (
    .S(or_2_out), .clk(or_4_out), .R(or_1_out), .Q(s_r_ff_2_q));  // open: Qn, preset, reset, en
  S_R_Flip_Flop #(.trigger("high")) s_r_ff_3 (
    .S(or_2_out), .clk(or_5_out), .R(or_1_out), .Q(s_r_ff_3_q));  // open: Qn, preset, reset, en
  S_R_Flip_Flop #(.trigger("high")) s_r_ff_4 (
    .S(or_2_out), .clk(or_6_out), .R(or_1_out), .Q(s_r_ff_4_q));  // open: Qn, preset, reset, en
  and and_1 (and_1_out, Zavreno, s_r_ff_1_q, s_r_ff_2_q, comparator_1_eq, comparator_2_eq, OK, comparator_3_eq, comparator_4_eq, s_r_ff_3_q, s_r_ff_4_q, Limit);
  Multiplexer #(.width(3), .enable("false")) multiplexer_1 (
    .in0(3'b000), .in1(3'b101), .out(_1__Cifra), .sel(s_r_ff_1_q));
  Multiplexer #(.width(3), .enable("false")) multiplexer_2 (
    .in0(3'b000), .in1(3'b101), .out(_2__Cifra), .sel(s_r_ff_2_q));
  Multiplexer #(.width(3), .enable("false")) multiplexer_3 (
    .in0(3'b000), .in1(3'b101), .out(_3__Cifra), .sel(s_r_ff_3_q));
  Multiplexer #(.width(3), .enable("false")) multiplexer_4 (
    .in0(3'b000), .in1(3'b101), .out(_4__Cifra), .sel(s_r_ff_4_q));
  T_Flip_Flop t_ff_1 (.clk(and_1_out), .T(and_1_out), .Q(\Odemknuto_Zamčeno ));  // open: Qn, preset, reset, en
  Counter #(.width(2), .max('h3), .ongoal("stay")) counter_2 (
    .Q(counter_2_q), .carry(counter_2_carry), .clk(and_2_out), .clr(or_7_out));  // open: load, D, count
  and and_2 (and_2_out, Zavreno, OK, s_r_ff_1_q, s_r_ff_2_q, s_r_ff_3_q, s_r_ff_4_q);
  or or_7 (or_7_out, Force_reset, \Odemknuto_Zamčeno );
  Multiplexer #(.width(3), .enable("false")) multiplexer_5 (
    .in0(3'b000), .in1(3'b111), .out(out_21), .sel(\Odemknuto_Zamčeno ));
  Subtractor #(.width(2)) subtractor_1 (.a(2'b11), .b(counter_2_q), .out(out_19[1:0]));  // open: bin, bout
  not not_1 (Limit, counter_2_carry);

  assign _1__Cifra_2 = {_1__Cifra[1], _1__Cifra[2:1]};
  assign _1__Cifra_3 = _1__Cifra;
  assign _2__Cifra_2 = {_2__Cifra[1], _2__Cifra[2:1]};
  assign _2__Cifra_3 = _2__Cifra;
  assign _3__Cifra_2 = {_3__Cifra[1], _3__Cifra[2:1]};
  assign _3__Cifra_3 = _3__Cifra;
  assign _4__Cifra_2 = {_4__Cifra[1], _4__Cifra[2:1]};
  assign _4__Cifra_3 = _4__Cifra;
  assign out_19[3:2] = 2'b00;
  assign out_22 = out_21;
  assign out_23 = out_21;
  assign out_24 = 3'b111;
  assign out_25 = 3'b111;
  assign out_26 = 3'b111;
endmodule

module _4bitmemory (
  input  [3:0] Input,
  input  Select,
  input  Write,
  input  RESET,
  output [3:0] out_5
);

  wire and_1_out, and_2_out, and_3_out, and_4_out, and_5_out, or_1_out, or_2_out, or_3_out, or_4_out;

  and and_1 (and_1_out, Select, Write);
  and and_2 (and_2_out, Input[0], and_1_out);
  and and_3 (and_3_out, Input[1], and_1_out);
  and and_4 (and_4_out, Input[2], and_1_out);
  and and_5 (and_5_out, Input[3], and_1_out);
  or or_1 (or_1_out, RESET, and_1_out);
  or or_2 (or_2_out, RESET, and_1_out);
  or or_3 (or_3_out, RESET, and_1_out);
  or or_4 (or_4_out, RESET, and_1_out);
  D_Flip_Flop d_ff_1 (.clk(or_1_out), .D(and_2_out), .Q(out_5[0]));  // open: Qn, preset, en, reset
  D_Flip_Flop d_ff_2 (.clk(or_2_out), .D(and_3_out), .Q(out_5[1]));  // open: Qn, preset, en, reset
  D_Flip_Flop d_ff_3 (.clk(or_3_out), .D(and_4_out), .Q(out_5[2]));  // open: Qn, preset, en, reset
  D_Flip_Flop d_ff_4 (.clk(or_4_out), .D(and_5_out), .Q(out_5[3]));  // open: Qn, preset, en, reset
endmodule

module CarDisplay (
  input  in_1,
  input  in_2,
  output [7:0] out_3,
  output [7:0] out_4,
  output [7:0] out_5,
  output [7:0] out_6,
  output [7:0] out_7,
  output [7:0] out_8,
  output [7:0] out_9,
  output [7:0] out_10,
  output [7:0] out_11,
  output [7:0] out_12,
  output [7:0] out_13,
  output [7:0] out_14,
  output [7:0] out_15,
  output [7:0] out_16,
  output [7:0] out_17,
  output [7:0] out_18,
  output [7:0] out_19,
  output [7:0] out_20,
  output [7:0] out_21,
  output [7:0] out_22,
  output [7:0] out_23,
  output [7:0] out_24,
  output [7:0] out_25,
  output [7:0] out_26,
  output [7:0] out_27,
  output [7:0] out_28,
  output [7:0] out_29,
  output [7:0] out_30
);

  wire and_1_out, and_2_out, and_3_out, clock_1_out, counter_1_carry, counter_2_carry, Kontrola, or_1_out,
       random_1_out;
  wire [3:0] counter_1_q;
  wire [7:0] multiplexer_1_out, multiplexer_2_out, multiplexer_3_out, shift_register_2_out;

  Clock clock_1 (.out(clock_1_out));
  Random #(.width(1)) random_1 (.clk(and_1_out), .out(random_1_out));  // open: next, clr
  Counter #(.width(4), .max('hf), .ongoal("stay")) counter_1 (
    .Q(counter_1_q), .carry(counter_1_carry), .clk(clock_1_out), .clr(and_1_out));  // open: load, D, count
  and and_1 (and_1_out, in_1, in_2);
  Multiplexer #(.select(4), .width(8), .enable("false")) multiplexer_1 (
    .in0(8'h1e), .in1(8'h27), .in2(8'h3f), .in3(8'h6), .in4(8'h3e), .in5(8'h3e), .in6(8'h3e), .in7(8'h3e),
    .in8(8'h3f), .in9(8'h3f), .in10(8'h3e), .in11({8{1'b0}}), .in12({8{1'b0}}), .in13({8{1'b0}}),
    .in14({8{1'b0}}), .in15({8{1'b0}}), .out(multiplexer_1_out), .sel(counter_1_q));
  Multiplexer #(.select(4), .width(8), .enable("false")) multiplexer_2 (
    .in0(8'h6), .in1(8'h7), .in2(8'h7), .in3(8'he), .in4(8'h16), .in5(8'h16), .in6(8'h16), .in7(8'hf),
    .in8(8'h7), .in9(8'he), .in10(8'h2), .in11({8{1'b0}}), .in12({8{1'b0}}), .in13({8{1'b0}}),
    .in14({8{1'b0}}), .in15({8{1'b0}}), .out(multiplexer_2_out), .sel(counter_1_q));
  Multiplexer #(.width(8), .enable("false")) multiplexer_3 (
    .in0(multiplexer_1_out), .in1(multiplexer_2_out), .out(multiplexer_3_out), .sel(random_1_out));
  Shift_Register #(.width(8), .length(13)) shift_register_1 (
    .shift(Kontrola), .in(multiplexer_3_out), .clk(clock_1_out), .q0(out_3), .q1(out_6), .q2(out_9),
    .q3(out_11), .q4(out_13), .q5(out_15), .q6(out_17), .q7(out_19), .q8(out_21), .q9(out_23), .q10(out_25),
    .q11(out_27), .q12(out_29));  // open: out, load, clr, d0, d1, d2, d3, d4, d5, d6, d7, d8, d9, d10, d11, d12
  Counter #(.width(4), .max('hc), .ongoal("stay")) counter_2 (
    .carry(counter_2_carry), .clk(clock_1_out), .clr(and_1_out));  // open: load, D, count, Q
  and and_2 (and_2_out, ~counter_2_carry, clock_1_out);  // AND_Gate
  and and_3 (and_3_out, clock_1_out, counter_1_carry);
  Shift_Register #(.width(8), .length(13)) shift_register_2 (
    .shift(Kontrola), .in(multiplexer_3_out), .clk(or_1_out), .out(shift_register_2_out));  // open: load, clr, d0, q0, d1, q1, d2, q2, d3, q3, d4, q4, d5, q5, d6, q6, d7, q7, d8, q8, d9, q9, d10, q10, d11, q11, d12, q12
  or or_1 (or_1_out, and_2_out, and_3_out);
  Shift_Register #(.width(8), .length(13)) shift_register_3 (
    .shift(Kontrola), .in(shift_register_2_out), .clk(clock_1_out), .q0(out_4), .q1(out_7), .q2(out_10),
    .q3(out_12), .q4(out_14), .q5(out_16), .q6(out_18), .q7(out_20), .q8(out_22), .q9(out_24), .q10(out_26),
    .q11(out_28), .q12(out_30));  // open: out, load, clr, d0, d1, d2, d3, d4, d5, d6, d7, d8, d9, d10, d11, d12
  Counter #(.width(5), .max('h1e), .ongoal("stay")) counter_3 (
    .carry(Kontrola), .clk(clock_1_out));  // open: load, D, count, Q, clr

  assign out_5 = {8{1'b1}};
  assign out_8 = {8{1'b1}};

  // Other names for the same wires on the sheet: _1[7:0] = out_3; _2[7:0] = out_6; _3[7:0] = out_9; _4[7:0] = out_11;
  //   _5[7:0] = out_13; _6[7:0] = out_15; _7[7:0] = out_17; _8[7:0] = out_19; _9[7:0] = out_21; _10[7:0] = out_23;
  //   _11[7:0] = out_25; _12[7:0] = out_27; _13[7:0] = out_29; _14[7:0] = out_4; _15[7:0] = out_7; _16[7:0] = out_10;
  //   _17[7:0] = out_12; _18[7:0] = out_14; _19[7:0] = out_16; _20[7:0] = out_18; _21[7:0] = out_20;
  //   _22[7:0] = out_22; _23[7:0] = out_24; _24[7:0] = out_26; _25[7:0] = out_28; _26[7:0] = out_30
endmodule

module CabelManagment (
  input  [15:0] in_1,
  input  [15:0] in_2,
  input  [15:0] in_3,
  input  [15:0] in_4,
  input  [15:0] in_5,
  input  [15:0] in_6,
  input  [15:0] in_7,
  input  [15:0] in_8,
  input  [15:0] in_9,
  input  [15:0] in_10,
  input  [15:0] in_11,
  input  [15:0] in_12,
  input  [15:0] in_13,
  input  [15:0] in_14,
  input  [15:0] in_15,
  input  [15:0] in_16,
  output [15:0] out_17,
  output [15:0] out_18,
  output [15:0] out_19,
  output [15:0] out_20,
  output [15:0] out_21,
  output [15:0] out_22,
  output [15:0] out_23,
  output [15:0] out_24,
  output [15:0] out_25,
  output [15:0] out_26,
  output [15:0] out_27,
  output [15:0] out_28,
  output [15:0] out_29,
  output [15:0] out_30,
  output [15:0] out_31,
  output [15:0] out_32
);


  assign out_17 = in_1;
  assign out_18 = in_2;
  assign out_19 = in_3;
  assign out_20 = in_4;
  assign out_21 = in_5;
  assign out_22 = in_6;
  assign out_23 = in_7;
  assign out_24 = in_8;
  assign out_25 = in_9;
  assign out_26 = in_10;
  assign out_27 = in_11;
  assign out_28 = in_12;
  assign out_29 = in_13;
  assign out_30 = in_14;
  assign out_31 = in_15;
  assign out_32 = in_16;
endmodule

module GateDisplaySystem (
  input  [15:0] in_1,
  input  [3:0] in_2,
  output [15:0] out_3
);

  Multiplexer #(.select(4), .width(16), .enable("false")) multiplexer_1 (
    .in0(in_1), .in1({in_1[14:0], 1'b0}), .in2({in_1[13:0], 2'b00}), .in3({in_1[12:0], 3'b000}),
    .in4({in_1[11:0], 4'b0000}), .in5({in_1[10:0], {5{1'b0}}}), .in6({in_1[9:0], {6{1'b0}}}),
    .in7({in_1[8:0], {7{1'b0}}}), .in8({in_1[7:0], {8{1'b0}}}), .in9({in_1[6:0], {9{1'b0}}}),
    .in10({in_1[5:0], {10{1'b0}}}), .in11({in_1[4:0], {11{1'b0}}}), .in12({in_1[3:0], {12{1'b0}}}),
    .in13({in_1[2:0], {13{1'b0}}}), .in14({in_1[1:0], {14{1'b0}}}), .in15({16{1'b0}}), .out(out_3), .sel(in_2));
endmodule

module GateDisplaySystem2 (
  input  [15:0] in_1,
  input  [3:0] in_2,
  output [15:0] out_3
);

  Multiplexer #(.select(4), .width(16), .enable("false")) multiplexer_1 (
    .in0(in_1), .in1({1'b0, in_1[15:1]}), .in2({2'b00, in_1[15:2]}), .in3({3'b000, in_1[15:3]}),
    .in4({4'b0000, in_1[15:4]}), .in5({{5{1'b0}}, in_1[15:5]}), .in6({{6{1'b0}}, in_1[15:6]}),
    .in7({{7{1'b0}}, in_1[15:7]}), .in8({{8{1'b0}}, in_1[15:8]}), .in9({{9{1'b0}}, in_1[15:9]}),
    .in10({{10{1'b0}}, in_1[15:10]}), .in11({{11{1'b0}}, in_1[15:11]}), .in12({{12{1'b0}}, in_1[15:12]}),
    .in13({{13{1'b0}}, in_1[15:13]}), .in14({{14{1'b0}}, in_1[15:14]}), .in15({16{1'b0}}), .out(out_3),
    .sel(in_2));
endmodule

module CabelManagment2 (
  input  [3:0] in_1,
  input  [3:0] in_2,
  input  [3:0] in_3,
  input  [3:0] in_4,
  input  in_5,
  input  in_6,
  output [3:0] out_7,
  output [3:0] out_8,
  output [3:0] out_9,
  output [3:0] out_10,
  output out_11,
  output out_12
);


  assign out_7 = in_1;
  assign out_8 = in_2;
  assign out_9 = in_3;
  assign out_10 = in_4;
  assign out_11 = in_5;
  assign out_12 = in_6;
endmodule

module LockSystemPassword (
  input  \Zamčeno ,
  input  in_2,
  input  _7,
  input  _8,
  input  _9,
  input  _4,
  input  _5,
  input  _6,
  input  _1,
  input  _2,
  input  _3,
  input  _0,
  input  OK,
  output [3:0] _1__Cifra,
  output [3:0] _2__Cifra,
  output Dioda,
  output [3:0] _3__Cifra,
  output [3:0] _4__Cifra
);

  wire and_1_out, and_2_out, and_3_out, demultiplexer_1_out0, demultiplexer_1_out1, demultiplexer_1_out2,
       demultiplexer_1_out3, or_1_out, or_2_out, t_ff_1_qn;
  wire [1:0] counter_1_q;
  wire [3:0] controlled_buffer_1_out;

  and and_1 (and_1_out, Dioda, OK);
  or or_1 (or_1_out, and_2_out, and_1_out);
  or or_2 (or_2_out, _2, _1, _4, _7, _0, _5, _8, _3, _6, _9);
  assign controlled_buffer_1_out = _9 ? 4'b1001 : 4'bz;  // Controlled_Buffer controlled_buffer_1
  assign controlled_buffer_1_out = _8 ? 4'b1000 : 4'bz;  // Controlled_Buffer controlled_buffer_2
  assign controlled_buffer_1_out = _7 ? 4'b0111 : 4'bz;  // Controlled_Buffer controlled_buffer_3
  assign controlled_buffer_1_out = _6 ? 4'b0110 : 4'bz;  // Controlled_Buffer controlled_buffer_4
  assign controlled_buffer_1_out = _5 ? 4'b0101 : 4'bz;  // Controlled_Buffer controlled_buffer_5
  assign controlled_buffer_1_out = _4 ? 4'b0100 : 4'bz;  // Controlled_Buffer controlled_buffer_6
  assign controlled_buffer_1_out = _3 ? 4'b0011 : 4'bz;  // Controlled_Buffer controlled_buffer_7
  assign controlled_buffer_1_out = _2 ? 4'b0010 : 4'bz;  // Controlled_Buffer controlled_buffer_8
  assign controlled_buffer_1_out = _1 ? 4'b0001 : 4'bz;  // Controlled_Buffer controlled_buffer_9
  assign controlled_buffer_1_out = _0 ? 4'b0000 : 4'bz;  // Controlled_Buffer controlled_buffer_10
  T_Flip_Flop t_ff_1 (.clk(or_1_out), .T(or_1_out), .Q(Dioda), .Qn(t_ff_1_qn));  // open: preset, reset, en
  and and_2 (and_2_out, in_2, \Zamčeno , t_ff_1_qn);
  and and_3 (and_3_out, or_2_out, Dioda);
  Demultiplexer #(.select(2), .enable("false")) demultiplexer_1 (
    .out0(demultiplexer_1_out0), .out1(demultiplexer_1_out1), .out2(demultiplexer_1_out2),
    .out3(demultiplexer_1_out3), .in(1'b1), .sel(counter_1_q));
  Counter #(.width(2), .max('h3), .trigger("falling")) counter_1 (
    .Q(counter_1_q), .clk(and_3_out), .clr(OK));  // open: load, D, count, carry
  _4bitmemory u_4bitmemory_1 (
    .out_5(_1__Cifra), .Input(controlled_buffer_1_out), .Select(demultiplexer_1_out0), .Write(and_3_out),
    .RESET(1'b0));
  _4bitmemory u_4bitmemory_2 (
    .out_5(_2__Cifra), .Input(controlled_buffer_1_out), .Select(demultiplexer_1_out1), .Write(and_3_out),
    .RESET(1'b0));
  _4bitmemory u_4bitmemory_3 (
    .out_5(_3__Cifra), .Input(controlled_buffer_1_out), .Select(demultiplexer_1_out2), .Write(and_3_out),
    .RESET(1'b0));
  _4bitmemory u_4bitmemory_4 (
    .out_5(_4__Cifra), .Input(controlled_buffer_1_out), .Select(demultiplexer_1_out3), .Write(and_3_out),
    .RESET(1'b0));
  Hex_Digit_Display hex_digit_display_1 (.value(_1__Cifra));  // open: dp
  Hex_Digit_Display hex_digit_display_2 (.value(_2__Cifra));  // open: dp
  Hex_Digit_Display hex_digit_display_3 (.value(_3__Cifra));  // open: dp
  Hex_Digit_Display hex_digit_display_4 (.value(_4__Cifra));  // open: dp

  // Notes on the sheet:
  //   Uložené Heslo
endmodule
